// Logisim project 10_Half_Adder.circ as structural Verilog: 1 circuit, main circuit Half adder
module Half_adder (
  input  A,
  input  B,
  output Sum,
  output Carry
);

  xor xor_1 (Sum, A, B);
  and and_1 (Carry, A, B);

  // Notes on the sheet:
  //   Half Adder
endmodule
