// Logisim project 12_Four_Bit_Adder.circ as structural Verilog: 2 circuits, main circuit 4-Bit-adder
module Full_Adder (
  input  A,
  input  B,
  input  Cin,
  output Sum,
  output Cout
);

  wire and_1_out, and_2_out, xor_1_out;

  xor xor_1 (xor_1_out, A, B);
  and and_1 (and_1_out, A, B);
  xor xor_2 (Sum, xor_1_out, Cin);
  and and_2 (and_2_out, xor_1_out, Cin);
  or or_1 (Cout, and_1_out, and_2_out);

  // Notes on the sheet:
  //   Full Adder
endmodule

module _4_Bit_adder (
  input  A0,
  input  B0,
  input  A1,
  input  A2,
  input  A3,
  input  Cin,
  input  B1,
  input  B2,
  input  B3,
  output out_10,
  output S1,
  output S2,
  output S3,
  output Cout
);

  wire full_adder_1_sum, full_adder_2_sum, full_adder_3_sum;

  Full_Adder full_adder_1 (.A(A0), .B(B0), .Cin(Cin), .Sum(full_adder_1_sum), .Cout(out_10));
  Full_Adder full_adder_2 (.A(A1), .B(B1), .Cin(full_adder_1_sum), .Sum(full_adder_2_sum), .Cout(S1));
  Full_Adder full_adder_3 (.A(A2), .B(B2), .Cin(full_adder_2_sum), .Sum(full_adder_3_sum), .Cout(S2));
  Full_Adder full_adder_4 (.A(A3), .B(B3), .Cin(full_adder_3_sum), .Sum(Cout), .Cout(S3));

  // Notes on the sheet:
  //   S0
  //   4-Bit Adder
endmodule
