// Logisim project 2_Basic_Gates.circ as structural Verilog
module Basic_Gates (
  input  in_1,
  input  in_2,
  input  in_3,
  input  in_4,
  input  in_5,
  output AND_gate,
  output out_7,
  output out_8
);

  and and_1 (AND_gate, in_1, in_2);
  or or_1 (out_7, in_3, in_4);
  not not_1 (out_8, in_5);

  // Notes on the sheet:
  //              OR gate
  //   NOT gate
endmodule
