// Logisim project 3_Universal_Gates.circ as structural Verilog: 1 circuit, main circuit Universal_Gates
module Universal_Gates (
  input  in_1,
  input  in_2,
  input  in_3,
  input  in_4,
  output out_5,
  output out_6
);

  nand nand_1 (out_5, in_1, in_2);
  nor nor_1 (out_6, in_3, in_4);

  // Notes on the sheet:
  //   NAND gate
  //      AND gate
endmodule
