// Logisim project 5_NOR_Universal.circ as structural Verilog: 1 circuit, main circuit NOR_Universal
module NOR_Universal (
  input  in_1,
  input  in_2,
  input  in_3,
  input  in_4,
  input  in_5,
  output NOT_using_NOR,
  output OR_using_NOR,
  output out_8
);

  wire nor_1_out, nor_2_out, nor_3_out;

  nor nor_1 (nor_1_out, in_2, in_3);
  nor nor_2 (nor_2_out, in_4, in_4);
  nor nor_3 (nor_3_out, in_5, in_5);
  nor nor_4 (NOT_using_NOR, in_1, in_1);
  nor nor_5 (OR_using_NOR, nor_1_out, nor_1_out);
  nor nor_6 (out_8, nor_2_out, nor_3_out);

  // Notes on the sheet:
  //   AND using NOR
endmodule
