// Logisim project 6_XOR.circ as structural Verilog: 1 circuit, main circuit XOR
module XOR (
  input  in_1,
  input  in_2,
  input  in_3,
  input  in_4,
  output XOR_Gate,
  output out_6
);

  wire and_1_out, and_2_out, not_1_out, not_2_out;

  not not_1 (not_1_out, in_3);
  not not_2 (not_2_out, in_4);
  xor xor_1 (XOR_Gate, in_1, in_2);
  and and_1 (and_1_out, not_1_out, in_4);
  and and_2 (and_2_out, in_3, not_2_out);
  or or_1 (out_6, and_1_out, and_2_out);

  // Notes on the sheet:
  //   XOR using AND and OR
endmodule
