// Logisim project 7_XNOR.circ as structural Verilog: 1 circuit, main circuit XNOR
module XNOR (
  input  in_1,
  input  in_2,
  input  in_3,
  input  in_4,
  output out_5,
  output out_6
);

  wire and_1_out, and_2_out, not_1_out, not_2_out;

  not not_1 (not_1_out, in_4);
  not not_2 (not_2_out, in_3);
  xnor xnor_1 (out_5, in_1, in_2);
  and and_1 (and_1_out, in_3, in_4);
  and and_2 (and_2_out, not_1_out, not_2_out);
  or or_1 (out_6, and_1_out, and_2_out);

  // Notes on the sheet:
  //   XNOR gate using AND and OR and NOT
  //   XNOR gate
endmodule
